# Fritzing sketch esp32C3oled-AHT20-BMP280 (saved by Fritzing 0.9.5d)
breadboards: 1

parts:
  A1 = ESP32-C3 0.42in OLED
  AHT1 = AHT20 BMP280 pressure and humidity breakout

nets:
  N1: A1.Pin_5, AHT1.SDA
  N2: A1.Pin_6, AHT1.SCL
  N3: A1.Pin_10, AHT1.GND
  N4: A1.Pin_11, AHT1.VDD

custom parts:
  ESP32-C3 0.42in OLED: ESP32-C3 0.42-Inch Oled White Light Display Bluetooth Development Board Type-C.
  AHT20 BMP280 pressure and humidity breakout: Cheap breakout board for the BMP280, barometric pressure sensor, and AHT20, humidity sensor
